# Fritzing sketch circuit (saved by Fritzing 1.0.7)
circuit board: 8.46667cm x 5.64444cm

parts:
  M1 = DOIT Esp32 DevKit v1 (30 pins long, 11 pins width) [part_number=ESP32S-PIN30]
  M2 = DOIT Esp32 DevKit v1 (30 pins long, 11 pins width) [part_number=ESP32S-PIN30]
  Mod1 = KY-005 Infrared Transmitter Module [package="Breakout board"]
  Mic1 = KY-038

nets:
  GND: M1.GND, M2.GND, Mod1.-, Mic1.pin2
  N1: M1.RX2, M2.TX2
  N2: M1.TX2, M2.RX2
  VIN: M1.VIN, M2.VIN, Mod1.Vin, Mic1.pin3
  N3: M2.D4, Mod1.S
  N4: M2.D34, Mic1.pin1

custom parts:
  DOIT Esp32 DevKit v1 (30 pins long, 11 pins width): The DOIT Esp32 DevKit v1 is one of the development board created by DOIT to evaluate the ESP-WROOM-32 module. It is based on the ESP32 microcontroller that boasts Wifi, Bluetooth, Ethernet and Low Power support all in a single chip. (vanepp) made breadboard work, adjusted pin numbering and labels and reduced size of schematic and cleaned up pcb. This chip is 30pins long (2 x15) and 11 pins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
  KY-005 Infrared Transmitter Module: Arduino IR Transmitter Module Keyes KY-005, emits infrared light at 38KHz.
  KY-038: ky-038 Microphone sound sensor module
